# Fritzing sketch inav-rangefinder (saved by Fritzing 0.9.3b)
breadboards: 1

parts:
  Arduino_Pro_Mini_3_3V = Arduino Pro Mini (3.3V)
  US-100_or_HC-SR04 = HC-SR04 Ultrasonic Rangemeter
  R1 = Resistor [tolerance=±5% resistance=1k package=THT]
  R2 = Resistor [tolerance=±5% resistance=1k package=THT]

nets:
  GND: Arduino_Pro_Mini_3_3V.GND, US-100_or_HC-SR04.GND
  SDA: Arduino_Pro_Mini_3_3V.A4
  SCL: Arduino_Pro_Mini_3_3V.A5
  +5V: Arduino_Pro_Mini_3_3V.RAW, US-100_or_HC-SR04.VCC
  N1: Arduino_Pro_Mini_3_3V.A2, R2.Pin_1
  N2: Arduino_Pro_Mini_3_3V.A1, R1.Pin_1
  N3: US-100_or_HC-SR04.Trig, R2.Pin_0
  N4: US-100_or_HC-SR04.Echo, R1.Pin_0
